// Logisim project project_2.circ as structural Verilog
module adder_half (
  input  a,
  input  b,
  output sum,
  output car
);

  xor xor_1 (sum, a, b);
  and and_1 (car, a, b);
endmodule

module adder_full (
  input  a,
  input  b,
  input  c,
  output sum,
  output car
);

  wire adder_half_1_car, adder_half_1_sum, adder_half_2_car;

  adder_half adder_half_1 (.a(a), .b(b), .sum(adder_half_1_sum), .car(adder_half_1_car));
  adder_half adder_half_2 (.a(adder_half_1_sum), .b(c), .sum(sum), .car(adder_half_2_car));
  or or_1 (car, adder_half_2_car, adder_half_1_car);
endmodule

module adder_4b (
  input  c,
  input  [3:0] a,
  input  [3:0] b,
  output [3:0] sum,
  output car
);

  wire adder_full_1_car, adder_full_2_car, adder_full_3_car;

  adder_full adder_full_1 (.a(a[0]), .b(b[0]), .c(c), .sum(sum[0]), .car(adder_full_1_car));
  adder_full adder_full_2 (.a(a[1]), .b(b[1]), .c(adder_full_1_car), .sum(sum[1]), .car(adder_full_2_car));
  adder_full adder_full_3 (.a(a[2]), .b(b[2]), .c(adder_full_2_car), .sum(sum[2]), .car(adder_full_3_car));
  adder_full adder_full_4 (.a(a[3]), .b(b[3]), .c(adder_full_3_car), .sum(sum[3]), .car(car));

  // Other names for the same wires on the sheet: a1 = a[0]; a2 = a[1]; a3 = a[2]; a4 = a[3]; b1 = b[0]; b2 = b[1];
  //   b3 = b[2]; b4 = b[3]; oc = car; o1 = sum[0]; o2 = sum[1]; o3 = sum[2]; o4 = sum[3]
endmodule

module adder_8b (
  input  c,
  input  [7:0] a,
  input  [7:0] b,
  output [7:0] sum,
  output car
);

  wire adder_4b_1_car;

  adder_4b adder_4b_1 (.a(a[3:0]), .b(b[3:0]), .c(c), .car(adder_4b_1_car), .sum(sum[3:0]));
  adder_4b adder_4b_2 (.a(a[7:4]), .b(b[7:4]), .c(adder_4b_1_car), .car(car), .sum(sum[7:4]));

  // Other names for the same wires on the sheet: a1[3:0] = a[3:0]; a2[3:0] = a[7:4]; b1[3:0] = b[3:0];
  //   b2[3:0] = b[7:4]
endmodule

module adder_16b (
  input  c,
  input  [15:0] a,
  input  [15:0] b,
  output [15:0] sum,
  output car
);

  wire adder_8b_1_car;

  adder_8b adder_8b_1 (.a(a[7:0]), .b(b[7:0]), .c(c), .sum(sum[7:0]), .car(adder_8b_1_car));
  adder_8b adder_8b_2 (.a(a[15:8]), .b(b[15:8]), .c(adder_8b_1_car), .sum(sum[15:8]), .car(car));

  // Other names for the same wires on the sheet: a1[7:0] = a[7:0]; a2[7:0] = a[15:8]; b1[7:0] = b[7:0];
  //   b2[7:0] = b[15:8]
endmodule
