// Logisim project project_3.circ as structural Verilog
module register_1b (
  input  i,
  input  l,
  output o
);

  wire clk_out, multiplexer_1_out, not_1_out;

  not not_1 (not_1_out, l);
  Multiplexer multiplexer_1 (.in0(i), .in1(o), .out(multiplexer_1_out), .sel(not_1_out));
  Clock clk (.out(clk_out));
  // Probe on o
  D_Flip_Flop d_ff_1 (.D(multiplexer_1_out), .clk(clk_out), .Q(o));  // open: Qn, preset, reset
endmodule

module register_16b (
  input  [15:0] i,
  input  load,
  output [15:0] o
);

  wire clck;

  Clock clock_1 (.out(clck));
  Register #(.width(1)) register_1 (.D(i[0]), .en(load), .clk(clck), .Q(o[0]));  // open: clr
  Register #(.width(1)) register_2 (.D(i[1]), .en(load), .clk(clck), .Q(o[1]));  // open: clr
  Register #(.width(1)) register_3 (.D(i[2]), .en(load), .clk(clck), .Q(o[2]));  // open: clr
  Register #(.width(1)) register_4 (.D(i[3]), .en(load), .clk(clck), .Q(o[3]));  // open: clr
  Register #(.width(1)) register_5 (.D(i[4]), .en(load), .clk(clck), .Q(o[4]));  // open: clr
  Register #(.width(1)) register_6 (.D(i[5]), .en(load), .clk(clck), .Q(o[5]));  // open: clr
  Register #(.width(1)) register_7 (.D(i[6]), .en(load), .clk(clck), .Q(o[6]));  // open: clr
  Register #(.width(1)) register_8 (.D(i[7]), .en(load), .clk(clck), .Q(o[7]));  // open: clr
  Register #(.width(1)) register_9 (.D(i[8]), .en(load), .clk(clck), .Q(o[8]));  // open: clr
  Register #(.width(1)) register_10 (.D(i[9]), .en(load), .clk(clck), .Q(o[9]));  // open: clr
  Register #(.width(1)) register_11 (.D(i[10]), .en(load), .clk(clck), .Q(o[10]));  // open: clr
  Register #(.width(1)) register_12 (.D(i[11]), .en(load), .clk(clck), .Q(o[11]));  // open: clr
  Register #(.width(1)) register_13 (.D(i[12]), .en(load), .clk(clck), .Q(o[12]));  // open: clr
  Register #(.width(1)) register_14 (.D(i[13]), .en(load), .clk(clck), .Q(o[13]));  // open: clr
  Register #(.width(1)) register_15 (.D(i[14]), .en(load), .clk(clck), .Q(o[14]));  // open: clr
  Register #(.width(1)) register_16 (.D(i[15]), .en(load), .clk(clck), .Q(o[15]));  // open: clr

  // Other names for the same wires on the sheet: ld = load
endmodule

module ram_4 (
  input  load,
  input  clock,
  input  [15:0] i,
  input  [1:0] addr,
  output [15:0] o
);

  wire demultiplexer_1_out0, demultiplexer_1_out1, demultiplexer_1_out2, demultiplexer_1_out3;
  wire [15:0] demultiplexer_2_out0, demultiplexer_2_out1, demultiplexer_2_out2, demultiplexer_2_out3,
       register_1_q, register_2_q, register_3_q, register_4_q;

  Demultiplexer #(.select(2)) demultiplexer_1 (
    .out0(demultiplexer_1_out0), .out1(demultiplexer_1_out1), .out2(demultiplexer_1_out2),
    .out3(demultiplexer_1_out3), .in(load), .sel(addr));
  Demultiplexer #(.select(2), .width(16)) demultiplexer_2 (
    .out0(demultiplexer_2_out0), .out1(demultiplexer_2_out1), .out2(demultiplexer_2_out2),
    .out3(demultiplexer_2_out3), .in(i), .sel(addr));
  Register #(.width(16)) register_1 (
    .D(demultiplexer_2_out0), .en(demultiplexer_1_out0), .clk(clock), .Q(register_1_q));  // open: clr
  Register #(.width(16)) register_2 (
    .D(demultiplexer_2_out1), .en(demultiplexer_1_out1), .clk(clock), .Q(register_2_q));  // open: clr
  Register #(.width(16)) register_3 (
    .D(demultiplexer_2_out2), .en(demultiplexer_1_out2), .clk(clock), .Q(register_3_q));  // open: clr
  Register #(.width(16)) register_4 (
    .D(demultiplexer_2_out3), .en(demultiplexer_1_out3), .clk(clock), .Q(register_4_q));  // open: clr
  Multiplexer #(.select(2), .width(16)) multiplexer_1 (
    .in0(register_1_q), .in1(register_2_q), .in2(register_3_q), .in3(register_4_q), .out(o), .sel(addr));

  // Other names for the same wires on the sheet: clck = clock
endmodule

module ram_8 (
  input  clock,
  input  [15:0] i,
  input  load,
  input  [2:0] addr,
  output [15:0] o
);

  wire demultiplexer_1_out0, demultiplexer_1_out1;
  wire [15:0] demultiplexer_2_out0, demultiplexer_2_out1, ram_4_1_o, ram_4_2_o;

  Demultiplexer demultiplexer_1 (.out0(demultiplexer_1_out0), .out1(demultiplexer_1_out1), .in(load), .sel(addr[2]));
  Demultiplexer #(.width(16)) demultiplexer_2 (
    .out0(demultiplexer_2_out0), .out1(demultiplexer_2_out1), .in(i), .sel(addr[2]));
  ram_4 ram_4_1 (.load(demultiplexer_1_out0), .clock(clock), .i(demultiplexer_2_out0), .addr(addr[1:0]), .o(ram_4_1_o));
  ram_4 ram_4_2 (.load(demultiplexer_1_out1), .clock(clock), .i(demultiplexer_2_out1), .addr(addr[1:0]), .o(ram_4_2_o));
  Multiplexer #(.width(16)) multiplexer_1 (.in0(ram_4_1_o), .in1(ram_4_2_o), .out(o), .sel(addr[2]));
endmodule
