// Logisim project project_5.circ as structural Verilog: 1 circuit, main circuit main
module main (
  input  [1:0] in_1,
  input  in_2,
  input  in_3,
  input  [3:0] in_4,
  output [3:0] out_5
);

  wire clock_1_out;

  Clock clock_1 (.out(clock_1_out));
  RAM #(.addrWidth(2), .clearpin("true"), .dataWidth(4), .\type ("nonvolatile")) ram_1 (
    .addr(in_1), .we(in_2), .oe(in_3), .clk(clock_1_out), .din(in_4), .dout(out_5));  // open: clr
endmodule
